# Fritzing sketch LED_protoShield (saved by Fritzing 0.9.0b)

parts:
  Part1 = Arduino Prototyping Shield
  Q1 = Basic FET N-Channel [package="TO220 [THT]"]
  Q2 = Basic FET N-Channel [package="TO220 [THT]"]
  Q3 = Basic FET N-Channel [package="TO220 [THT]"]
  R1 = Resistor [tolerance=±5% resistance=10k package=THT]
  R2 = Resistor [tolerance=±5% resistance=10k package=THT]
  R3 = Resistor [tolerance=±5% resistance=10k package=THT]
  LED1 = RGB LED - (4 legs) [package="5 mm [THT]"]
  BAT1 = BC9VPC [package=bc9vpc]
  S1 = Pushbutton [package="[THT]"]
  S3 = Pushbutton [package="[THT]"]
  R4 = Resistor [tolerance=±5% resistance=10k package=THT]
  R5 = Resistor [tolerance=±5% resistance=10k package=THT]

nets:
  N1: Part1.+5V, Part1.N$398, Part1.N$400, Part1.N$427, Part1.N$431, S1.Pin_1, S1.Pin_2, S3.Pin_1, S3.Pin_2
  N2: Part1.GND, Part1.N$272, Part1.N$319, Q1.source, Q3.source, R1.Pin_0, R2.Pin_0, R3.Pin_0, BAT1.V-, R4.Pin_1, R5.Pin_1
  N3: Part1.D9, Part1.N$59, Part1.N$297, Q3.gate, R3.Pin_1
  N4: Part1.D10, Part1.N$83, Part1.N$261, Q2.gate, R2.Pin_1
  N5: Part1.D11, Part1.N$107, Q1.gate, R1.Pin_1
  N6: Part1.N$26, Part1.N$79, Part1.N$393, S3.Pin_3, S3.Pin_4, R4.Pin_0
  N7: Part1.N$72, Part1.N$263, Q2.source
  N8: Part1.N$87, Part1.N$405, Part1.N$409, S1.Pin_3, S1.Pin_4, R5.Pin_0
  N9: Part1.N$105, Part1.N$299, Q3.drain, LED1.red_cathode
  N10: Part1.N$106, Part1.N$324, Q1.drain, LED1.blue_cathode
  N11: Part1.N$262, Part1.N$322, Q2.drain, LED1.green_cathode
  N12: Part1.N$321, LED1.common_anode, BAT1.V+
