# Fritzing sketch mega-dat-config (saved by Fritzing 0.9.0b)
breadboards: 1

parts:
  Part1 = Arduino Mega 2560 (Rev3)
  Q1 = MOSFET-NCHANNEL [package=to220v]
  Q2 = MOSFET-NCHANNEL [package=to220v]
  Q3 = MOSFET-NCHANNEL [package=to220v]
  S1 = Pushbutton [package="[THT]"]
  R2 = Resistor [tolerance=±5% resistance=10k package="0805 [SMD]"]
  R3 = Resistor [tolerance=±5% resistance=10k package="0805 [SMD]"]
  R4 = Resistor [tolerance=±5% resistance=10k package="0805 [SMD]"]
  R5 = Resistor [tolerance=±5% resistance=10k package="0805 [SMD]"]
  LED1 = RGB LED (com. cathode, rgb) [package="5 mm [THT]"]
  INA1 = INA219 DC Current Sensor Breakout

nets:
  N1: Part1.A5, Part1.A6
  N2: Part1.D21/SCL, INA1.SCL
  N3: Part1.D20/SDA, INA1.SDA
  N4: Part1.D13_PWM, Part1.D10_PWM
  5V: Part1.5V, S1.Pin_3, S1.Pin_4, INA1.VCC
  GND: Part1.GND, Q1.S, Q2.S, Q3.S, R2.Pin_1, R4.Pin_1, R5.Pin_1, INA1.GND
  N5: Part1.D5_PWM, Q3.G, R4.Pin_0
  N6: Part1.D6_PWM, Q1.G, R5.Pin_0
  N7: Part1.D7_PWM, Q2.G, R2.Pin_0
  N8: Part1.D52, S1.Pin_1, S1.Pin_2, R3.Pin_0
  N9: Q1.D, LED1.green_anode
  N10: Q2.D, LED1.red_anode
  N11: Q3.D, LED1.common_cathode

custom parts:
  INA219 DC Current Sensor Breakout: INA DC Current Sensor Breakout
