# Fritzing sketch DM_LED_PCB (saved by Fritzing 0.9.0b)
circuit board: 6.88566cm x 5.36311cm
breadboards: 1

parts:
  Red_Mosfet = Basic FET N-Channel [package="TO220 [THT]"]
  Blue_Mosfet = Basic FET N-Channel [package="TO220 [THT]"]
  Blue_Mosfet_Pulldown = Resistor [tolerance=±5% resistance=10k package=THT]
  Green_Mosfet_Pulldown = Resistor [tolerance=±5% resistance=10k package=THT]
  Red_Mosfet_Pulldown = Resistor [tolerance=±5% resistance=10k package=THT]
  Button_3 = Pushbutton [package="[THT]"]
  Button_2_Pulldown = Resistor [tolerance=±5% resistance=10k package=THT]
  Button_3_Pulldown = Resistor [tolerance=±5% resistance=10k package=THT]
  Button_2 = Pushbutton [package="[THT]"]
  Green_Mosfet = Basic FET N-Channel [package="TO220 [THT]"]
  Part1 = Arduino Uno (Rev3)

nets:
  N1: Red_Mosfet.gate, Red_Mosfet_Pulldown.Pin_1, Part1.D9_PWM
  N2: Blue_Mosfet.gate, Blue_Mosfet_Pulldown.Pin_1, Part1.D11_PWM/MOSI
  N3: Blue_Mosfet_Pulldown.Pin_0, Green_Mosfet_Pulldown.Pin_0, Red_Mosfet_Pulldown.Pin_0, Button_2_Pulldown.Pin_0, Button_3_Pulldown.Pin_0, Part1.GND
  N4: Green_Mosfet_Pulldown.Pin_1, Green_Mosfet.source, Part1.D10_PWM/SS
  N5: Button_3.Pin_1, Button_3.Pin_2, Button_2.Pin_1, Button_2.Pin_2, Part1.5V
  N6: Button_3.Pin_3, Button_3.Pin_4, Button_2_Pulldown.Pin_1, Part1.D3_PWM
  N7: Button_3_Pulldown.Pin_1, Button_2.Pin_3, Button_2.Pin_4, Part1.D2
