# Fritzing sketch Mega_halfbb (saved by Fritzing 0.9.0b)
breadboards: 1

parts:
  Part1 = Arduino Mega 2560 (Rev3)
  Q1 = MOSFET-NCHANNEL [package=to220v]
  Q2 = MOSFET-NCHANNEL [package=to220v]
  Q3 = MOSFET-NCHANNEL [package=to220v]
  LED1 = RGB LED (com. cathode, rgb) [package="5 mm [THT]"]
  U1 = LIPO-2000mAh [package=lipo-2000]
  S1 = Pushbutton [package="[THT]"]
  R1 = Resistor [tolerance=±5% resistance=10k package="0805 [SMD]"]
  R2 = Resistor [tolerance=±5% resistance=10k package="0805 [SMD]"]
  R3 = Resistor [tolerance=±5% resistance=10k package="0805 [SMD]"]
  R4 = Resistor [tolerance=±5% resistance=10k package="0805 [SMD]"]
  JACK2 = 2.1mm DC Barrel Jack
  JACK3 = 2.1mm Barrel Jack with Terminal Block

nets:
  N1: Part1.D11_PWM, Q2.G, R3.Pin_0
  N2: Part1.D10_PWM, Q1.G, R2.Pin_0
  N3: Part1.D9_PWM, Q3.G, R1.Pin_0
  N4: Part1.5V, S1.Pin_1, S1.Pin_2
  N5: Part1.GND, R1.Pin_1, R2.Pin_1, R3.Pin_1, R4.Pin_1, JACK2.center
  N6: Part1.D52, S1.Pin_3, S1.Pin_4, R4.Pin_0
  N7: Q1.D, LED1.green_anode
  N8: Q2.D, LED1.blue_anode
  N9: Q3.D, LED1.red_anode
  N10: LED1.common_cathode, JACK2.switch
  N11: U1.+, JACK3.POS
  N12: U1.-, JACK3.NEG

custom parts:
  2.1mm DC Barrel Jack: 2.1mm DC Barrel Jack with Thru-Hole Connectors (breadboardable)
