# Fritzing sketch LEDControlCircuit (saved by Fritzing 0.8.7b)
breadboards: 1

parts:
  Part1 = Arduino Uno (Rev3)
  Q1 = Basic FET P-Channel [package="TO220 [THT]"]  # not connected
  BAT1 = BC9VPC [package=bc9vpc]
  Q2 = Basic FET P-Channel [package="TO220 [THT]"]  # not connected
  Q3 = Basic FET P-Channel [package="TO220 [THT]"]  # not connected
  LED1 = RGB LED (com. anode, rbg) [package="5 mm [THT]"]

nets:
  N1: Part1.GND, BAT1.V+
  N2: BAT1.V-, LED1.common_anode
